// Logisim project miniprocessador8bits.circ as structural Verilog: 4 circuits, main circuit main
module main (
  input  [15:0] in_1,
  input  in_2,
  input  [15:0] in_3,
  input  in_4,
  input  in_5,
  input  [14:0] in_6,
  input  in_7,
  input  [15:0] in_8,
  input  in_9,
  input  in_10,
  output [15:0] out_11,
  output [11:0] out_12,
  output [15:0] out_13,
  output [15:0] out_14,
  output [15:0] out_15,
  output [15:0] out_16,
  output [2:0] out_17,
  output [15:0] out_18,
  output [2:0] out_19,
  output [15:0] out_20,
  output [2:0] out_21
);

  wire alu_1_zero, and_1_out, clock_1_out, clock_2_out, control_1_alusrc, control_1_branch,
       control_1_jalsuport, control_1_jump, control_1_jumpreg, control_1_memread, control_1_memtoreg,
       control_1_memwrite, control_1_regdst, control_1_regwrite;
  wire [1:0] control_1_aluop;
  wire [3:0] multiplexer_1_out, multiplexer_2_out;
  wire [15:0] adder_1_out, adder_2_out, adder_3_out, multiplexer_3_out, multiplexer_4_out, multiplexer_5_out,
       multiplexer_6_out, register_1_q, registradores_1_read_data_1, registradores_1_read_data_2;

  Clock clock_1 (.out(clock_1_out));
  Register #(.width(16)) register_1 (
    .D(multiplexer_5_out), .Q(register_1_q), .clk(clock_1_out), .clr(in_10));  // open: en
  ROM #(.addrWidth(16), .dataWidth(16)) rom_1 (.addr(register_1_q), .data({out_20[15:12], out_12}));
  Adder #(.width(16)) adder_1 (.a(16'h1), .b(register_1_q), .out(adder_1_out));  // open: cin, cout
  assign out_11 = {{4{out_12[11]}}, out_12};  // Bit_Extender bit_extender_1
  Adder #(.width(16)) adder_2 (.a(out_11), .b(in_1), .out(adder_2_out));  // open: cin, cout
  Control control_1 (
    .A(out_20[15]), .B(out_20[14]), .C(out_20[13]), .D(out_20[12]), .RegWrite(control_1_regwrite),
    .RegDst(control_1_regdst), .Alusrc(control_1_alusrc), .MemRead(control_1_memread),
    .AluOp(control_1_aluop), .Branch(control_1_branch), .Jump(control_1_jump), .MemToReg(control_1_memtoreg),
    .MemWrite(control_1_memwrite), .JumpReg(control_1_jumpreg), .JalSuport(control_1_jalsuport));
  Multiplexer #(.width(4)) multiplexer_1 (
    .in0({in_7, out_12[8:6]}), .in1({in_9, out_12[5:3]}), .out(multiplexer_1_out), .sel(control_1_regdst));
  Multiplexer #(.width(4)) multiplexer_2 (
    .in0(multiplexer_1_out), .in1(4'b0111), .out(multiplexer_2_out), .sel(control_1_jalsuport));
  assign out_16 = {{10{out_12[5]}}, out_12[5:0]};  // Bit_Extender bit_extender_2
  Registradores registradores_1 (
    .Clock(clock_1_out), .ReadReg1({in_5, out_12[11:9]}), .ReadReg2({in_7, out_12[8:6]}),
    .WriteReg(multiplexer_2_out), .WriteData(out_15), .RegWrite(control_1_regwrite),
    .Read_data_1(registradores_1_read_data_1), .Read_data_2(registradores_1_read_data_2));
  Multiplexer #(.width(16)) multiplexer_3 (
    .in0(registradores_1_read_data_2), .in1(out_16), .out(multiplexer_3_out), .sel(control_1_alusrc));
  ALU alu_1 (
    .in_1(registradores_1_read_data_1), .in_2(multiplexer_3_out), .in_3(in_6), .Control(control_1_aluop),
    .OpCode(out_20[15:12]), .ZERO(alu_1_zero), .ALUResult(out_18));
  Adder #(.width(16)) adder_3 (.a(adder_1_out), .b(out_16), .out(adder_3_out));  // open: cin, cout
  and and_1 (and_1_out, control_1_branch, alu_1_zero);
  RAM #(.addrWidth(16), .dataWidth(16), .enables("line")) ram_1 (
    .addr(out_18), .we(control_1_memwrite), .clk(clock_1_out), .din(registradores_1_read_data_2),
    .dout(out_14));
  Multiplexer #(.width(16)) multiplexer_4 (
    .in0(adder_1_out), .in1(adder_3_out), .out(multiplexer_4_out), .sel(and_1_out));
  Multiplexer #(.width(16)) multiplexer_5 (
    .in0(multiplexer_4_out), .in1(adder_2_out), .out(multiplexer_5_out), .sel(control_1_jump));
  Multiplexer #(.width(16)) multiplexer_6 (
    .in0(out_18), .in1(out_14), .out(multiplexer_6_out), .sel(control_1_memtoreg));
  Multiplexer #(.width(16)) multiplexer_7 (
    .in0(multiplexer_6_out), .in1(adder_1_out), .out(out_15), .sel(control_1_jalsuport));
  Clock clock_2 (.out(clock_2_out));
  RAM #(.addrWidth(16), .dataWidth(16)) ram_2 (
    .addr(in_3), .oe(in_4), .clk(clock_2_out), .din(in_8), .dout(out_13));  // open: we

  assign out_20[11:0] = out_12;

  // Notes on the sheet:
  //   contents of rom_1 (hex, n*v repeats v):
  //   8086 8040 44d1 30c1 8700 f006 31c1 4c1 41ff 329 3181 4b84 44ff 36c1 8700 f006 3840 36c1 8700 f006
endmodule

module Registradores (
  input  Clock,
  input  [3:0] ReadReg1,
  input  [3:0] ReadReg2,
  input  [3:0] WriteReg,
  input  [15:0] WriteData,
  input  RegWrite,
  output [15:0] Read_data_1,
  output [15:0] Read_data_2
);

  wire and_1_out, and_2_out, and_3_out, and_4_out, and_5_out, and_6_out, and_7_out, and_8_out, and_9_out,
       and_10_out, and_11_out, and_12_out, and_13_out, and_14_out, and_15_out, and_16_out, decoder_1_out0,
       decoder_1_out1, decoder_1_out2, decoder_1_out3, decoder_1_out4, decoder_1_out5, decoder_1_out6,
       decoder_1_out7, decoder_1_out8, decoder_1_out9, decoder_1_out10, decoder_1_out11, decoder_1_out12,
       decoder_1_out13, decoder_1_out14, decoder_1_out15;
  wire [15:0] register_1_q, register_2_q, register_3_q, register_4_q, register_5_q, register_6_q,
       register_7_q, register_8_q, register_9_q, register_10_q, register_11_q, register_12_q, register_13_q,
       register_14_q, register_15_q, register_16_q;

  Decoder #(.select(4)) decoder_1 (
    .out0(decoder_1_out0), .out1(decoder_1_out1), .out2(decoder_1_out2), .out3(decoder_1_out3),
    .out4(decoder_1_out4), .out5(decoder_1_out5), .out6(decoder_1_out6), .out7(decoder_1_out7),
    .out8(decoder_1_out8), .out9(decoder_1_out9), .out10(decoder_1_out10), .out11(decoder_1_out11),
    .out12(decoder_1_out12), .out13(decoder_1_out13), .out14(decoder_1_out14), .out15(decoder_1_out15),
    .sel(WriteReg));  // open: en
  and and_1 (and_1_out, decoder_1_out0, RegWrite);
  and and_2 (and_2_out, decoder_1_out1, RegWrite);
  and and_3 (and_3_out, decoder_1_out2, RegWrite);
  and and_4 (and_4_out, decoder_1_out3, RegWrite);
  and and_5 (and_5_out, decoder_1_out4, RegWrite);
  and and_6 (and_6_out, decoder_1_out5, RegWrite);
  and and_7 (and_7_out, decoder_1_out6, RegWrite);
  and and_8 (and_8_out, decoder_1_out7, RegWrite);
  and and_9 (and_9_out, decoder_1_out8, RegWrite);
  and and_10 (and_10_out, decoder_1_out9, RegWrite);
  and and_11 (and_11_out, decoder_1_out10, RegWrite);
  and and_12 (and_12_out, decoder_1_out11, RegWrite);
  and and_13 (and_13_out, decoder_1_out12, RegWrite);
  and and_14 (and_14_out, decoder_1_out13, RegWrite);
  and and_15 (and_15_out, decoder_1_out14, RegWrite);
  and and_16 (and_16_out, decoder_1_out15, RegWrite);
  Register #(.width(16)) register_1 (.D(WriteData), .en(and_1_out), .Q(register_1_q), .clk(Clock));  // open: clr
  Register #(.width(16)) register_2 (.D(WriteData), .en(and_2_out), .Q(register_2_q), .clk(Clock));  // open: clr
  Register #(.width(16)) register_3 (.D(WriteData), .en(and_3_out), .Q(register_3_q), .clk(Clock));  // open: clr
  Register #(.width(16)) register_4 (.D(WriteData), .en(and_4_out), .Q(register_4_q), .clk(Clock));  // open: clr
  Register #(.width(16)) register_5 (.D(WriteData), .en(and_5_out), .Q(register_5_q), .clk(Clock));  // open: clr
  Register #(.width(16)) register_6 (.D(WriteData), .en(and_6_out), .Q(register_6_q), .clk(Clock));  // open: clr
  Register #(.width(16)) register_7 (.D(WriteData), .en(and_7_out), .Q(register_7_q), .clk(Clock));  // open: clr
  Register #(.width(16)) register_8 (.D(WriteData), .en(and_8_out), .Q(register_8_q), .clk(Clock));  // open: clr
  Register #(.width(16)) register_9 (.D(WriteData), .en(and_9_out), .Q(register_9_q), .clk(Clock));  // open: clr
  Register #(.width(16)) register_10 (.D(WriteData), .en(and_10_out), .Q(register_10_q), .clk(Clock));  // open: clr
  Register #(.width(16)) register_11 (.D(WriteData), .en(and_11_out), .Q(register_11_q), .clk(Clock));  // open: clr
  Register #(.width(16)) register_12 (.D(WriteData), .en(and_12_out), .Q(register_12_q), .clk(Clock));  // open: clr
  Register #(.width(16)) register_13 (.D(WriteData), .en(and_13_out), .Q(register_13_q), .clk(Clock));  // open: clr
  Register #(.width(16)) register_14 (.D(WriteData), .en(and_14_out), .Q(register_14_q), .clk(Clock));  // open: clr
  Register #(.width(16)) register_15 (.D(WriteData), .en(and_15_out), .Q(register_15_q), .clk(Clock));  // open: clr
  Register #(.width(16)) register_16 (.D(WriteData), .en(and_16_out), .Q(register_16_q), .clk(Clock));  // open: clr
  Multiplexer #(.disabled("Z"), .enable("true"), .select(4), .width(16)) multiplexer_1 (
    .in0(register_1_q), .in1(register_2_q), .in2(register_3_q), .in3(register_4_q), .in4(register_5_q),
    .in5(register_6_q), .in6(register_7_q), .in7(register_8_q), .in8(register_9_q), .in9(register_10_q),
    .in10(register_11_q), .in11(register_12_q), .in12(register_13_q), .in13(register_14_q),
    .in14(register_15_q), .in15(register_16_q), .out(Read_data_1), .sel(ReadReg1));  // open: en
  Multiplexer #(.disabled("Z"), .enable("true"), .select(4), .width(16)) multiplexer_2 (
    .in0(register_1_q), .in1(register_2_q), .in2(register_3_q), .in3(register_4_q), .in4(register_5_q),
    .in5(register_6_q), .in6(register_7_q), .in7(register_8_q), .in8(register_9_q), .in9(register_10_q),
    .in10(register_11_q), .in11(register_12_q), .in12(register_13_q), .in13(register_14_q),
    .in14(register_15_q), .in15(register_16_q), .out(Read_data_2), .sel(ReadReg2));  // open: en
endmodule

module Control (
  input  A,
  input  B,
  input  C,
  input  D,
  output RegWrite,
  output RegDst,
  output Alusrc,
  output MemRead,
  output [1:0] AluOp,
  output Branch,
  output Jump,
  output MemToReg,
  output MemWrite,
  output JumpReg,
  output JalSuport
);

  wire and_1_out, and_2_out, and_3_out, and_4_out, and_5_out, not_1_out, not_3_out, not_4_out;

  not not_1 (not_1_out, A);
  not not_2 (RegWrite, B);
  not not_3 (not_3_out, C);
  not not_4 (not_4_out, D);
  and and_1 (and_1_out, not_1_out, not_4_out);
  and and_2 (and_2_out, A, RegWrite, C);
  and and_3 (and_3_out, not_1_out, D);
  and and_4 (and_4_out, not_3_out, D);
  and and_5 (and_5_out, A, RegWrite);
  and and_6 (MemRead, A, not_3_out);
  and and_7 (AluOp[0], not_1_out, not_3_out);
  and and_8 (Branch, not_1_out, B);
  and and_9 (Jump, A, D);
  and and_10 (MemToReg, A, RegWrite);
  and and_11 (JumpReg, B, C, not_4_out);
  and and_12 (JalSuport, A, RegWrite, C);
  or or_1 (RegDst, and_1_out, and_2_out);
  or or_2 (Alusrc, and_3_out, and_4_out, and_5_out);

  assign AluOp[1] = 1'b0;
  assign MemWrite = 1'b0;
endmodule

module ALU (
  input  [15:0] in_1,
  input  [15:0] in_2,
  input  [14:0] in_3,
  input  [1:0] Control,
  input  [3:0] OpCode,
  output ZERO,
  output [15:0] ALUResult
);

  wire and_2_out, and_3_out, comparator_1_eq, comparator_1_gt, comparator_1_lt;
  wire [0:0] and_1_out;
  wire [15:0] adder_1_out, multiplexer_1_out, subtractor_1_out;

  Comparator #(.width(16)) comparator_1 (
    .a(in_1), .b(in_2), .gt(comparator_1_gt), .eq(comparator_1_eq), .lt(comparator_1_lt));
  Adder #(.width(16)) adder_1 (.a(in_1), .b(in_2), .out(adder_1_out));  // open: cin, cout
  Subtractor #(.width(16)) subtractor_1 (.a(in_2), .b(in_1), .out(subtractor_1_out));  // open: bin, bout
  and and_1 (and_1_out[0], ~comparator_1_gt, ~comparator_1_eq, comparator_1_lt);  // AND_Gate
  Multiplexer #(.width(16)) multiplexer_1 (
    .in0(adder_1_out), .in1(subtractor_1_out), .out(multiplexer_1_out), .sel(and_2_out));
  and and_2 (and_2_out, ~Control[1], Control[0]);  // AND_Gate
  Multiplexer #(.width(16)) multiplexer_2 (
    .in0(multiplexer_1_out), .in1({in_3, and_1_out[0]}), .out(ALUResult), .sel(and_3_out));
  and and_3 (and_3_out, ~OpCode[3], ~OpCode[2], ~OpCode[1], ~OpCode[0]);  // AND_Gate
  and and_4 (ZERO, ~multiplexer_1_out[0], ~multiplexer_1_out[1], ~multiplexer_1_out[2], ~multiplexer_1_out[3], ~multiplexer_1_out[4], ~multiplexer_1_out[5], ~multiplexer_1_out[6], ~multiplexer_1_out[7], ~multiplexer_1_out[8], ~multiplexer_1_out[9], ~multiplexer_1_out[10], ~multiplexer_1_out[11], ~multiplexer_1_out[12], ~multiplexer_1_out[13], ~multiplexer_1_out[14], ~multiplexer_1_out[15]);  // AND_Gate
endmodule
